# Fritzing sketch Breadboard (saved by Fritzing 0.9.3b)
breadboards: 1

parts:
  R1 = Resistor [tolerance=±5% resistance=22k package=THT]
  R2 = Resistor [tolerance=±5% resistance=10k package=THT]
  R3 = Resistor [tolerance=±5% resistance=10k package=THT]
  U1 = NodeMCU V1.0
  Grove1 = Catalex 4 Digit Display
  J1 = Piezo Speaker
  S1 = Pushbutton [package="[THT]"]
  R4 = Resistor [tolerance=±5% resistance=10k package=THT]
  U3 = TP4056 [chip_label=TP4056]
  U4 = Voltage Regulator - 3.3V [package="TO220 [THT]"]

nets:
  N1: R1.Pin_0, R3.Pin_1
  N2: R1.Pin_1, U3.connector1, U4.output_voltage
  N3: R2.Pin_1, R3.Pin_0, U1.A0
  N4: U1.D0, J1.pin2
  N5: U1.D1, S1.Pin_3, S1.Pin_4, R4.Pin_0
  N6: U1.D3, U1.SD3
  N7: U1.3V3, S1.Pin_1, S1.Pin_2, U4.input_voltage
  GND: U1.GND, Grove1.GND, J1.pin1, R4.Pin_1, U3.connector2, U4.GND
  N8: U1.D5, Grove1.VCC
  N9: U1.D6, Grove1.DIO
  N10: U1.D7, Grove1.CLK
  N11: U1.Vin, U3.connector4

custom parts:
  NodeMCU V1.0: ESP8266 based NodeMCU
  Catalex 4 Digit Display: A 4 7-seg display
